# Fritzing sketch feather_MCP23017 (saved by Fritzing 0.9.9b)
breadboards: 1

parts:
  IC1 = MCP23017 I2C I/O Expander
  Part3 = Adafruit Feather HUZZAH ESP8266 [part_number="Adafruit #2821"]
  R1 = Resistor [tolerance=±5% power=0.25 resistance=10k package=THT]
  R2 = Resistor [tolerance=±5% power=0.25 resistance=10k package=THT]
  R3 = Resistor [tolerance=±5% power=0.25 resistance=10k package=THT]
  LED2 = LED - 5mm [color="Red (633nm)" current=0.030 package="5 mm [THT]"]
  LED1 = LED - 5mm [color="Blue (470nm)" current=0.030 package="5 mm [THT]"]
  Switch1 = Pushbutton [package="[SMD]"]
  Switch2 = Pushbutton [package="[SMD]"]

nets:
  N1: IC1.GPB0, LED2.anode
  N2: IC1.GPB1, LED1.anode
  VDD: IC1.VDD, Part3.3.3V, R1.Pin_1, R2.Pin_1, R3.Pin_0
  VSS: IC1.VSS, IC1.A0, IC1.A1, IC1.A2, Part3.GND, LED2.cathode, LED1.cathode, Switch1.Pin_1, Switch1.Pin_2, Switch2.Pin_1, Switch2.Pin_2
  N3: IC1.SCL, Part3.GPIO5/SCL, R1.Pin_0
  N4: IC1.SDA, Part3.GPIO4/SDA, R2.Pin_0
  N5: IC1.RESET, R3.Pin_1
  N6: IC1.GPA4, Switch1.Pin_3, Switch1.Pin_4
  N7: IC1.GPA7, Switch2.Pin_3, Switch2.Pin_4

custom parts:
  MCP23017 I2C I/O Expander: The MCP23017 uses two i2c pins (these can be shared with other i2c devices), and in exchange gives you 16 general purpose pins. You can set each of 16 pins to be input, output, input with a pullup or open drain. There's even the ability to get an interrupt via an external pin when any of the inputs change so you don't have to keep polling the chip.
  Adafruit Feather HUZZAH ESP8266: his is the Adafruit Feather HUZZAH ESP8266 - our take on an 'all-in-one' ESP8266 WiFi development board with built in USB and battery charging. Its an ESP8266 WiFi module with all the extras you need, ready to rock! We have other boards in the Feather family, check'em out here. At the Feather HUZZAH's heart is an ESP8266 WiFi microcontroller clocked at 80 MHz and at 3.3V logic. This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
